// Logisim project cpu.circ as structural Verilog
module _10_bit_Register_File (
  input  [9:0] Write_Data,
  input  [1:0] RS,
  input  [1:0] RD,
  input  WE,
  input  in_5,
  input  [1:0] RT,
  output [9:0] Data_1,
  output [9:0] Data_2
);

  wire and_1_out, and_2_out, and_3_out, and_4_out, decoder_1_out0, decoder_1_out1, decoder_1_out2,
       decoder_1_out3;
  wire [9:0] register_1_q, register_2_q, register_3_q, register_4_q;

  Decoder #(.select(2), .enable("false")) decoder_1 (
    .out0(decoder_1_out0), .out1(decoder_1_out1), .out2(decoder_1_out2), .out3(decoder_1_out3), .sel(RD));
  and and_1 (and_1_out, decoder_1_out0, WE);
  and and_2 (and_2_out, decoder_1_out1, WE);
  and and_3 (and_3_out, decoder_1_out2, WE);
  and and_4 (and_4_out, decoder_1_out3, WE);
  Register #(.width(10)) register_1 (.D(Write_Data), .en(and_1_out), .Q(register_1_q), .clk(in_5));  // open: clr
  Register #(.width(10)) register_2 (.D(Write_Data), .en(and_2_out), .Q(register_2_q), .clk(in_5));  // open: clr
  Register #(.width(10)) register_3 (.D(Write_Data), .en(and_3_out), .Q(register_3_q), .clk(in_5));  // open: clr
  Register #(.width(10)) register_4 (.D(Write_Data), .en(and_4_out), .Q(register_4_q), .clk(in_5));  // open: clr
  Multiplexer #(.select(2), .width(10), .enable("false")) multiplexer_1 (
    .in0(register_1_q), .in1(register_2_q), .in2(register_3_q), .in3(register_4_q), .out(Data_1), .sel(RS));
  Multiplexer #(.select(2), .width(10), .enable("false")) multiplexer_2 (
    .in0(register_1_q), .in1(register_2_q), .in2(register_3_q), .in3(register_4_q), .out(Data_2), .sel(RT));
endmodule

module _1_Bit_ALU (
  input  B,
  input  A,
  input  Cin,
  input  A_in,
  input  B_in,
  input  [1:0] alu_op,
  output out_7,
  output out_8
);

  wire adder_1_out, and_1_out, multiplexer_1_out, multiplexer_2_out, not_1_out, not_2_out, or_1_out;

  not not_1 (not_1_out, B);
  Multiplexer #(.enable("false")) multiplexer_1 (.in0(B), .in1(not_1_out), .out(multiplexer_1_out), .sel(B_in));
  not not_2 (not_2_out, A);
  Multiplexer #(.enable("false")) multiplexer_2 (.in0(A), .in1(not_2_out), .out(multiplexer_2_out), .sel(A_in));
  and and_1 (and_1_out, multiplexer_2_out, multiplexer_1_out);
  or or_1 (or_1_out, multiplexer_2_out, multiplexer_1_out);
  Adder #(.width(1)) adder_1 (.a(multiplexer_2_out), .b(multiplexer_1_out), .out(adder_1_out), .cin(Cin), .cout(out_8));
  Multiplexer #(.select(2), .enable("false")) multiplexer_3 (
    .in0(and_1_out), .in1(or_1_out), .in2(adder_1_out), .out(out_7), .sel(alu_op));  // open: in3
endmodule

module _10_bit_ALU (
  input  A_in,
  input  B_in,
  input  [1:0] ALU_OP,
  input  [9:0] A,
  input  C_in,
  input  [9:0] B,
  output [9:0] ALU_out,
  output Zero,
  output OverFlow,
  output Cout
);

  wire n1_bit_alu_1_out_8, n1_bit_alu_2_out_8, n1_bit_alu_3_out_8, n1_bit_alu_4_out_8, n1_bit_alu_5_out_8,
       n1_bit_alu_6_out_8, n1_bit_alu_7_out_8, n1_bit_alu_8_out_8, n1_bit_alu_9_out_8;

  _1_Bit_ALU u_1_bit_alu_1 (
    .A_in(A_in), .B_in(B_in), .alu_op(ALU_OP), .out_7(ALU_out[0]), .out_8(n1_bit_alu_1_out_8), .B(B[0]),
    .A(A[0]), .Cin(C_in));
  _1_Bit_ALU u_1_bit_alu_2 (
    .A_in(A_in), .B_in(B_in), .alu_op(ALU_OP), .out_7(ALU_out[1]), .out_8(n1_bit_alu_2_out_8), .B(B[1]),
    .A(A[1]), .Cin(n1_bit_alu_1_out_8));
  _1_Bit_ALU u_1_bit_alu_3 (
    .A_in(A_in), .B_in(B_in), .alu_op(ALU_OP), .out_7(ALU_out[2]), .out_8(n1_bit_alu_3_out_8), .B(B[2]),
    .A(A[2]), .Cin(n1_bit_alu_2_out_8));
  _1_Bit_ALU u_1_bit_alu_4 (
    .A_in(A_in), .B_in(B_in), .alu_op(ALU_OP), .out_7(ALU_out[3]), .out_8(n1_bit_alu_4_out_8), .B(B[3]),
    .A(A[3]), .Cin(n1_bit_alu_3_out_8));
  _1_Bit_ALU u_1_bit_alu_5 (
    .A_in(A_in), .B_in(B_in), .alu_op(ALU_OP), .out_7(ALU_out[4]), .out_8(n1_bit_alu_5_out_8), .B(B[4]),
    .A(A[4]), .Cin(n1_bit_alu_4_out_8));
  _1_Bit_ALU u_1_bit_alu_6 (
    .A_in(A_in), .B_in(B_in), .alu_op(ALU_OP), .out_7(ALU_out[5]), .out_8(n1_bit_alu_6_out_8), .B(B[5]),
    .A(A[5]), .Cin(n1_bit_alu_5_out_8));
  _1_Bit_ALU u_1_bit_alu_7 (
    .A_in(A_in), .B_in(B_in), .alu_op(ALU_OP), .out_7(ALU_out[6]), .out_8(n1_bit_alu_7_out_8), .B(B[6]),
    .A(A[6]), .Cin(n1_bit_alu_6_out_8));
  _1_Bit_ALU u_1_bit_alu_8 (
    .A_in(A_in), .B_in(B_in), .alu_op(ALU_OP), .out_7(ALU_out[7]), .out_8(n1_bit_alu_8_out_8), .B(B[7]),
    .A(A[7]), .Cin(n1_bit_alu_7_out_8));
  _1_Bit_ALU u_1_bit_alu_9 (
    .A_in(A_in), .B_in(B_in), .alu_op(ALU_OP), .out_7(ALU_out[8]), .out_8(n1_bit_alu_9_out_8), .B(B[8]),
    .A(A[8]), .Cin(n1_bit_alu_8_out_8));
  _1_Bit_ALU u_1_bit_alu_10 (
    .A_in(A_in), .B_in(B_in), .alu_op(ALU_OP), .out_7(ALU_out[9]), .out_8(Cout), .B(B[9]), .A(A[9]),
    .Cin(n1_bit_alu_9_out_8));
  nor nor_1 (Zero, ALU_out[0], ALU_out[1], ALU_out[2], ALU_out[3], ALU_out[4], ALU_out[5], ALU_out[6], ALU_out[7], ALU_out[8], ALU_out[9]);
  or or_1 (OverFlow, n1_bit_alu_9_out_8, Cout);
endmodule

module R_Type (
  input  in_1,
  input  in_2,
  input  in_3,
  input  in_4,
  input  [1:0] ALU_OP,
  output [3:0] out_6,
  output [9:0] out_7,
  output [9:0] out_8,
  output out_9,
  output out_10,
  output out_11,
  output [9:0] out_12
);

  wire clock_1_out;
  wire [5:0] ram_1_data;
  wire [9:0] adder_1_out, register_1_q;

  Clock clock_1 (.out(clock_1_out));
  Adder #(.width(10)) adder_1 (.a(register_1_q), .b(10'h1), .out(adder_1_out));  // open: cin, cout
  Register #(.width(10)) register_1 (.D(adder_1_out), .Q(register_1_q), .clk(clock_1_out));  // open: en, clr
  RAM #(.addrWidth(10), .dataWidth(10)) ram_1 (
    .addr(register_1_q), .data({out_6, ram_1_data}), .clk(clock_1_out));  // open: sel, ld, clr
  _10_bit_Register_File u_10_bit_register_file_1 (
    .WE(in_4), .in_5(clock_1_out), .Data_1(out_7), .RS(ram_1_data[5:4]), .Data_2(out_12),
    .RT(ram_1_data[3:2]), .Write_Data(out_8), .RD(ram_1_data[1:0]));
  _10_bit_ALU u_10_bit_alu_1 (
    .A(out_7), .B(out_12), .ALU_out(out_8), .Zero(out_9), .OverFlow(out_10), .Cout(out_11), .A_in(in_1),
    .B_in(in_2), .ALU_OP(ALU_OP), .C_in(in_3));
endmodule

module I_Type (
  input  in_1,
  input  in_2,
  input  in_3,
  input  clear,
  input  mem_read,
  input  mem_write,
  input  in_7,
  input  clolck,
  output [9:0] out_9,
  output [9:0] out_10,
  output [9:0] out_11,
  output [9:0] out_12,
  output out_13,
  output out_14,
  output out_15,
  output [9:0] out_16,
  output [9:0] out_17
);

  wire [1:0] bit_extender_2_out;
  wire [9:0] adder_1_out, register_1_q;

  Register #(.width(10)) register_1 (.D(adder_1_out), .Q(register_1_q), .clk(clolck), .clr(clear));  // open: en
  Adder #(.width(10)) adder_1 (.a(register_1_q), .b(10'h1), .out(adder_1_out));  // open: cin, cout
  ROM #(.addrWidth(10), .dataWidth(10)) rom_1 (.addr(register_1_q), .data(out_10));  // open: sel
  _10_bit_Register_File u_10_bit_register_file_1 (
    .WE(in_7), .in_5(clolck), .Data_1(out_9), .RS(out_10[7:6]), .Data_2(out_16), .RT(out_10[5:4]),
    .Write_Data(out_12), .RD(out_10[5:4]));
  assign out_17 = {{6{1'b0}}, out_10[3:0]};  // Bit_Extender bit_extender_1
  _10_bit_ALU u_10_bit_alu_1 (
    .A(out_9), .B(out_17), .ALU_out(out_11), .Zero(out_13), .OverFlow(out_14), .Cout(out_15), .A_in(in_1),
    .B_in(in_2), .ALU_OP(out_10[9:8]), .C_in(in_3));
  Bit_Extender #(.in_width(10), .out_width(2)) bit_extender_2 (.in(out_11), .out(bit_extender_2_out));
  RAM #(.addrWidth(2), .dataWidth(10), .bus("separate")) ram_1 (
    .addr(bit_extender_2_out), .din(out_16), .data(out_12), .str(mem_read), .clk(clolck), .ld(mem_write));  // open: sel, clr

  // Notes on the sheet:
  //   contents of rom_1 (hex, n*v repeats v):
  //   61 60
endmodule

module Instruction_Fetch (
  input  clear,
  output [9:0] out_2
);

  wire clock_1_out;
  wire [9:0] adder_1_out, register_1_q;

  Clock clock_1 (.out(clock_1_out));
  Register #(.width(10)) register_1 (.D(adder_1_out), .Q(register_1_q), .clk(clock_1_out), .clr(clear));  // open: en
  Adder #(.width(10)) adder_1 (.a(register_1_q), .b(10'h1), .out(adder_1_out));  // open: cin, cout
  ROM #(.addrWidth(10), .dataWidth(10)) rom_1 (.addr(register_1_q), .data(out_2));  // open: sel

  // Notes on the sheet:
  //   contents of rom_1 (hex, n*v repeats v):
  //   5f 4e 11
endmodule
